# Fritzing sketch KeyPad (saved by Fritzing 0.9.3b)
circuit board: 4.2cm x 1.5cm

parts:
  S1 = Pushbutton [package="[THT]"]
  S2 = Pushbutton [package="[THT]"]
  S3 = Pushbutton [package="[THT]"]
  JP1 = M16 [package=1x16_machine-pin-header_lock.004]
  JP2 = Header 4 [package=1x04-smd]

nets:
  GND: S1.Pin_1, S2.Pin_1, S3.Pin_1, S3.Pin_2, JP1.14, JP1.15, JP2.1
  GPIO14: S1.Pin_3, S1.Pin_4, JP1.7
  GPIO12: S2.Pin_3, S2.Pin_4, JP1.8
  GPIO13: S3.Pin_3, S3.Pin_4, JP1.9
  EN: JP1.1
  GPIO16: JP1.2
  GPIO5: JP1.3, JP2.2
  GPIO4: JP1.4, JP2.3
  GPIO0: JP1.5
  GPIO2: JP1.6
  GIPO3: JP1.11
  GPIO1: JP1.12
  3.3V: JP1.13
  5V: JP1.16, JP2.4
